// Logisim project bitAdder.circ as structural Verilog: 1 circuit, main circuit main
module main (
  input  in_1,
  input  in_2,
  input  in_3,
  input  in_4,
  input  in_5,
  input  in_6,
  input  in_7,
  input  in_8,
  input  in_9,
  output out_10,
  output out_11,
  output out_12,
  output out_13,
  output out_14,
  output out_15,
  output out_16
);

  wire and_2_out, and_3_out, and_4_out, and_5_out, and_6_out, or_2_out, xor_3_out, xor_5_out;

  and and_1 (out_10, in_1, in_2, in_2);
  xor xor_1 (out_11, in_1, in_2);
  and and_2 (and_2_out, in_3, in_4, in_4);
  xor xor_2 (out_13, in_3, in_4);
  and and_3 (and_3_out, in_6, in_7, in_7);
  xor xor_3 (xor_3_out, in_6, in_7);
  and and_4 (and_4_out, in_5, out_13);
  xor xor_4 (out_14, in_5, out_13);
  and and_5 (and_5_out, xor_3_out, in_8);
  xor xor_5 (xor_5_out, in_8, xor_3_out);
  or or_1 (out_12, and_2_out, and_4_out);
  or or_2 (or_2_out, and_3_out, and_5_out);
  and and_6 (and_6_out, xor_5_out, in_9, in_9);
  xor xor_6 (out_16, xor_5_out, in_9);
  or or_3 (out_15, or_2_out, and_6_out);

  // Notes on the sheet:
  //   half adder
endmodule
